# Fritzing sketch amg sketch (saved by Fritzing 0.9.10b)

parts:
  M1 = DOIT Esp32 DevKit v1 (30 pins long, 11 pins width) [part_number=ESP32S-PIN30]
  S1 = Round Pushbutton
  S2 = Round Pushbutton
  S3 = Square Pushbutton
  S4 = Square Pushbutton
  S6 = Round Pushbutton
  S7 = Round Pushbutton
  S8 = Round Pushbutton
  S9 = Round Pushbutton
  S10 = Round Pushbutton
  S11 = Round Pushbutton
  S12 = Round Pushbutton
  S13 = JOYSTICK_MINI_ALI [package=joystick_mini]

nets:
  N1: M1.GND, S13.LEFT
  N2: M1.D4, S7.leg1, S9.leg1
  N3: M1.D5, S4.leg1, S6.leg1, S11.leg1
  N4: M1.D18, S8.leg1, S10.leg1
  N5: M1.D19, S1.leg1, S2.leg1, S12.leg1
  N6: M1.D21, S2.leg0
  N7: M1.D22, S1.leg0, S6.leg0, S7.leg0, S10.leg0
  N8: M1.D23, S8.leg0, S9.leg0, S11.leg0, S12.leg0
  N9: M1.D26, S13.CENT
  N10: M1.D27, S13.UP
  N11: M1.D14, S13.GND
  N12: M1.D12, S13.RIGHT
  N13: M1.D13, S13.DOWN
  N14: S3.leg0, S4.leg0

custom parts:
  DOIT Esp32 DevKit v1 (30 pins long, 11 pins width): The DOIT Esp32 DevKit v1 is one of the development board created by DOIT to evaluate the ESP-WROOM-32 module. It is based on the ESP32 microcontroller that boasts Wifi, Bluetooth, Ethernet and Low Power support all in a single chip. (vanepp) made breadboard work, adjusted pin numbering and labels and reduced size of schematic and cleaned up pcb. This chip is 30pins long (2 x15) and 11 pins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
  JOYSTICK_MINI_ALI: Small 5-way tactile joystick, COM-10063 4UCON SF303GJ26
